# Fritzing sketch connection_scheme (saved by Fritzing 0.9.5d)
perfboards: 1

parts:
  8_4V_->_5V = LM2596 step down module
  Wheel_1 = DC Motor
  Battery_2 = battery_holder_single_18650
  2s_BMS = 2S-BMS
  U1 = OV7670 Camera [package=camera_sfv24r-2st_2]
  Side_sensor = hc_sro4
  Forward_sensor = hc_sro4
  M1 = DOIT Esp32 DevKit v1 (30 pins long, 11 pins width) [part_number=ESP32S]
  Type-C_Charger = USB_MICROB_PLUG [package=micro-b-smt]
  A1 = MX1508
  Wheel_2 = DC Motor
  Battery_1 = battery_holder_single_18650
  Компонент1 = Adafruit INA219 [part_number=1]
  Компонент2 = InvenSense MPU6050
  D1 = Diode [package=diode-1n4148]
  U2 = A3144 Hall Effect Sensor. [package="UA [THT]"]
  S1 = SWITCH-MOMENTARY-2 [package=tactile-pth-12mm]
  D2 = Diode [package=diode-1n4148]

nets:
  N1: 8_4V_->_5V.IN+, S1.2
  GND: 8_4V_->_5V.IN-, 8_4V_->_5V.OUT-, 2s_BMS.pin3#2, U1.GND, Side_sensor.GND, Forward_sensor.GND, M1.GND, Type-C_Charger.GND, A1.Pin_2, Компонент1.GND, Компонент1.VIN-, Компонент2.GND, U2.GND
  N2: 8_4V_->_5V.OUT+, D1.A, U2.+Vsupply, D2.A
  N3: Wheel_1.pin_1, A1.Pin_10
  N4: Wheel_1.pin_2, A1.Pin_9
  N5: Battery_2.+#0, 2s_BMS.pin1
  N6: Battery_2.+#1, 2s_BMS.pin3#4, Battery_1.+#0
  N7: 2s_BMS.pin2, Battery_1.+#1
  N8: 2s_BMS.pin3#3, Type-C_Charger.VCC, Компонент1.VIN+, S1.1
  3V3: U1.3V3, M1.3V3, Компонент1.VCC, Компонент2.VCC
  N9: U1.SIOC, M1.D22, Компонент1.SCL, Компонент2.SCL
  N10: U1.VSYNC, M1.D34
  N11: U1.PCLK, M1.D33
  N12: U1.D7, M1.D2
  N13: U1.D5, M1.D13
  N14: U1.D3, M1.D15
  N15: U1.D1, M1.TX2
  N16: U1.SIDO, M1.D21, Компонент1.SDA, Компонент2.SDA
  N17: U1.HREF, M1.D35
  N18: U1.XCLK, M1.D32
  N19: U1.D6, M1.D12
  N20: U1.D4, M1.D14
  N21: U1.D2, M1.RX2
  N22: U1.D0, M1.D27
  VCC: Side_sensor.VCC, Forward_sensor.VCC, D1.C
  N23: Side_sensor.Trig, Forward_sensor.Trig, M1.D23
  N24: Side_sensor.Echo, M1.D25
  N25: Forward_sensor.Echo, M1.VN
  N26: M1.D4, A1.Pin_6
  N27: M1.D5, A1.Pin_5
  N28: M1.D18, A1.Pin_4
  N29: M1.D19, A1.Pin_3
  N30: M1.D26, U2.Out
  N31: A1.Pin_1, D2.C
  N32: A1.Pin_7, Wheel_2.pin_2
  N33: A1.Pin_8, Wheel_2.pin_1

custom parts:
  LM2596 step down module: LM2596 DC-DC step down power supply module 3 A.
  battery_holder_single_18650: single 18650 battery holder
  2S-BMS: 2S-BMS LIPO battery charger / protection unit. Note pcb does not match the board as it will likely connect with wires, so pcb is 5 pads suitable for .1in header pins.
  OV7670 Camera: CMOS image sensor
  DOIT Esp32 DevKit v1 (30 pins long, 11 pins width): The DOIT Esp32 DevKit v1 is one of the development board created by DOIT to evaluate the ESP-WROOM-32 module. It is based on the ESP32 microcontroller that boasts Wifi, Bluetooth, Ethernet and Low Power support all in a single chip. (vanepp) made breadboard work, adjusted pin numbering and labels and reduced size of schematic and cleaned up pcb. This chip is 30pins long (2 x15) and 11 pins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
  MX1508: MX1508 DC Motor Driver is a low-cost motor driver module that can control DC stepper motors of current rating up to 2A.
  Adafruit INA219: This breakout board will solve all your power-monitoring problems. Instead of struggling with two multimeters, you can just use the handy INA219B chip on this breakout to both measure both the high side voltage and DC current draw over I2C with 1% precision. Most current-measuring devices such as our current panel meter are only good for low side measuring. That means that unless you want to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
  A3144 Hall Effect Sensor.: Allegro A3144 hall effect switch for high temperature operation.

// code stored in the sketch: washer.ino

